# Fritzing sketch led_with_switch (saved by Fritzing 1.0.1rc)
breadboards: 1

parts:
  VCC1 = Battery block 9V
  R1 = Resistor [tolerance=±5% power=0.25W resistance=1k package=THT]
  S1 = Pushbutton [package="[THT]"]
  LED1 = LED - 5mm [color="Red (633nm)" current=0.030A package="5 mm [THT]"]

nets:
  N1: VCC1.-, R1.Pin_0
  N2: VCC1.+, LED1.anode
  N3: R1.Pin_1, S1.Pin_1, S1.Pin_2, LED1.cathode
  N4: S1.Pin_3, S1.Pin_4
