# Fritzing sketch analog-read-poti (saved by Fritzing 1.0.1rc)

parts:
  Bauteil2 = Arduino Uno (Rev3) - ICSP
  R3 = Rotary Potentiometer (Small) [maximum_resistance=10kΩ knob_status=50% power=0.5W package=THT]

nets:
  N1: Bauteil2.A0, R3.wiper
  N2: Bauteil2.5V, R3.leg2
  N3: Bauteil2.GND, R3.leg1
