# Fritzing sketch led-frequency-with-poti (saved by Fritzing 1.0.1rc)
breadboards: 1

parts:
  Bauteil2 = Arduino Uno (Rev3) - ICSP
  R2 = Resistor [tolerance=±5% power=0.25W resistance=1k package=THT]
  LED2 = LED - 5mm [color="Red (633nm)" current=0.030A package="5 mm [THT]"]
  R3 = Rotary Potentiometer (Small) [maximum_resistance=10kΩ knob_status=50% power=0.5W package=THT]

nets:
  N1: Bauteil2.A0, R3.wiper
  N2: Bauteil2.D13/SCK, R2.Pin_1, R3.leg2
  N3: Bauteil2.GND, LED2.cathode, R3.leg1
  N4: R2.Pin_0, LED2.anode
