# Fritzing sketch h-bridge-with-flyback (saved by Fritzing 1.0.1rc)
circuit board: 6.85273cm x 5.00957cm
breadboards: 1

parts:
  R1 = Resistor [tolerance=±5% power=0.25W resistance=330 package=THT]
  R1_2 = Resistor [tolerance=±5% power=0.25W resistance=10k package=THT]
  R2 = Resistor [tolerance=±5% power=0.25W resistance=330 package=THT]
  R3 = Resistor [tolerance=±5% power=0.25W resistance=10k package=THT]
  R5 = Resistor [tolerance=±5% power=0.25W resistance=330 package=THT]
  R6 = Resistor [tolerance=±5% power=0.25W resistance=330 package=THT]
  R7 = Resistor [tolerance=±5% power=0.25W resistance=10k package=THT]
  Q2 = Basic FET N-Channel [package="TO220 [THT]"]
  Q4 = Basic FET N-Channel [package="TO220 [THT]"]
  Q1 = Basic FET P-Channel [package="TO220 [THT]"]
  Q3 = Basic FET P-Channel [package="TO220 [THT]"]
  T2 = NPN-Transistor [package="TO92 [THT]"]
  J1 = male pin header, 6 pins [form="♂ (male)"]
  J2 = Screw terminal - 2 pins [package=THT]
  R4 = Resistor [tolerance=±5% power=0.25W resistance=10k package=THT]
  T1 = NPN-Transistor [package="TO92 [THT]"]
  D1 = Diode [package=diode-1n4001]
  D2 = Diode [package=diode-1n4001]
  D3 = Diode [package=diode-1n4001]
  D4 = Diode [package=diode-1n4001]

nets:
  N1: R1.Pin_0, T1.C
  N2: R1.Pin_1, Q1.gate, R4.Pin_1
  N3: R1_2.Pin_0, Q2.gate, J1.pin4
  GND: R1_2.Pin_1, R3.Pin_1, Q2.source, Q4.source, T2.E, J1.pin1, T1.E, D2.A, D4.A
  N4: R2.Pin_0, J1.pin5
  N5: R2.Pin_1, T1.B
  N6: R3.Pin_0, Q4.gate, J1.pin2
  N7: R5.Pin_0, J1.pin3
  N8: R5.Pin_1, T2.B
  N9: R6.Pin_0, T2.C
  N10: R6.Pin_1, R7.Pin_1, Q3.gate
  N11: R7.Pin_0, Q1.drain, Q3.drain, J1.pin6, R4.Pin_0, D1.C, D3.C
  N12: Q2.drain, Q1.source, J2.pin2, D1.A, D2.C
  N13: Q4.drain, Q3.source, J2.pin1, D3.A, D4.C
