# Fritzing sketch h-bridge (saved by Fritzing 1.0.1rc)
breadboards: 1

parts:
  Q2 = Basic FET N-Channel [package="D2Pak [SMD]"]
  Q1 = Basic FET P-Channel [package="DPak [SMD]"]
  Q4 = Basic FET N-Channel [package="D2Pak [SMD]"]
  Q3 = Basic FET P-Channel [package="DPak [SMD]"]
  T1 = NPN-Transistor [package="SOT-23 [SMD]"]
  T2 = NPN-Transistor [package="SOT-23 [SMD]"]
  R1 = Resistor [tolerance=±5% power=0.25W resistance=330 package=THT]
  R1_2 = Resistor [tolerance=±5% power=0.25W resistance=10k package=THT]
  J1 = male pin header, 5 pins [form="♂ (male)"]
  R2 = Resistor [tolerance=±5% power=0.25W resistance=330 package=THT]
  R3 = Resistor [tolerance=±5% power=0.25W resistance=10k package=THT]
  R4 = Resistor [tolerance=±5% power=0.25W resistance=10k package=THT]
  R5 = Resistor [tolerance=±5% power=0.25W resistance=330 package=THT]
  J2 = male pin header, 2 pins [form="♂ (male)"]
  R6 = Resistor [tolerance=±5% power=0.25W resistance=330 package=THT]
  R7 = Resistor [tolerance=±5% power=0.25W resistance=10k package=THT]

nets:
  N1: Q2.Gate, R1_2.Pin_0, J1.pin4
  N2: Q2.drain, Q1.source, J2.pin2
  GND: Q2.source, Q4.source, T1.2, T2.2, R1_2.Pin_1, J1.pin1, R3.Pin_1
  N3: Q1.Gate, R1.Pin_1, R4.Pin_1
  12V: Q1.drain, Q3.drain, R4.Pin_0, R7.Pin_0
  N4: Q4.Gate, J1.pin2, R3.Pin_0
  N5: Q4.drain, Q3.source, J2.pin1
  N6: Q3.Gate, R6.Pin_1, R7.Pin_1
  N7: T1.0, R2.Pin_1
  N8: T1.1, R1.Pin_0
  N9: T2.0, R5.Pin_1
  N10: T2.1, R6.Pin_0
  N11: J1.pin3, R5.Pin_0
  N12: J1.pin5, R2.Pin_0
