# Fritzing sketch ir_dedetctor (saved by Fritzing 1.0.1rc)

parts:
  M3 = fc-51 [package=THT]
  Bauteil1 = Arduino Uno (Rev3) - ICSP

nets:
  N1: M3.pin1, Bauteil1.D11_PWM/MOSI
  N2: M3.pin2, Bauteil1.GND
  N3: M3.pin3, Bauteil1.5V
