# Fritzing sketch line_follow_robot (saved by Fritzing 1.0.1rc)
breadboards: 1

parts:
  bread = Arduino Uno (Rev3) - ICSP
  S1 = H-Bridge with L298N
  M1 = gear-motor
  M2 = fc-51 [package=THT]
  M3 = fc-51 [package=THT]
  M4 = gear-motor
  U1 = SWITCH-SPST-2 [package=switch-spst-vertical]
  VCC1 = 4 x AAA Battery Mount

nets:
  N1: bread.ICSP_MISO, bread.D12/MISO, M2.pin1
  N2: bread.D8, S1.IN2
  N3: bread.D9_PWM, S1.IN3
  N4: bread.D10_PWM/SS, S1.IN4
  N5: bread.D11_PWM/MOSI, M3.pin1
  N6: bread.D5_PWM, S1.ENB
  N7: bread.D6_PWM, S1.ENA
  N8: bread.D7, S1.IN1
  5V: bread.5V, S1.5V, M2.pin3, M3.pin3
  GND: bread.GND, S1.GND, M2.pin2, M3.pin2, VCC1.-
  N9: S1.12V, U1.O
  N10: S1.M1-01, M1.pin_2
  N11: S1.M1-02, M1.pin_1
  N12: S1.M2-01, M4.pin_2
  N13: S1.M2-02, M4.pin_1
  N14: U1.P, VCC1.+

custom parts:
  H-Bridge with L298N: h-bridge
