# Fritzing sketch dht-22 (saved by Fritzing 1.0.1rc)
breadboards: 1

parts:
  Bauteil2 = Arduino Uno (Rev3) - ICSP
  DHT1 = DHT22 Humidity and Temperature Sensor
  R1 = Resistor [tolerance=±5% power=0.25W resistance=10k package=THT]

nets:
  N1: Bauteil2.D4, DHT1.DATA, R1.Pin_1
  5V: Bauteil2.5V, DHT1.VDD, R1.Pin_0
  GND: Bauteil2.GND, DHT1.GND
